# Fritzing sketch 3led (saved by Fritzing 0.9.3b)
breadboards: 1

parts:
  LED1 = LEDs [package=led10mm]
  LED2 = LEDs [package=led10mm]
  LED3 = LEDs [package=led10mm]
  U1 = LuaNode32 / ESP32 [part_number=ESP32S-PIN30]
  R1 = Resistor [tolerance=±5% resistance=220 package=THT]
  R2 = Resistor [tolerance=±5% resistance=220 package=THT]
  R3 = Resistor [tolerance=±5% resistance=220 package=THT]

nets:
  N1: LED1.C, LED2.C, LED3.C, U1.GND
  N2: LED1.A, R1.Pin_1
  N3: LED2.A, R2.Pin_1
  N4: LED3.A, R3.Pin_1
  N5: U1.D18, R1.Pin_0
  N6: U1.D19, R2.Pin_0
  N7: U1.D21, R3.Pin_0

custom parts:
  LuaNode32 / ESP32: New Image for LuaNode32 DOIT ESP32 DEVKIT V1. Base parts from LuaNode32 / ESP32 ESP32 based LuaNode32 by G.Noorlander DOIT Esp32 DevKit v1 (30 pins long, 11 pins width) by Werner Rothschopf (modified by vanepp Dec 2018)
