# Fritzing sketch OLED (saved by Fritzing 0.9.3b)
breadboards: 1

parts:
  Grove1 = Grove OLED 128x96
  U1 = LuaNode32 / ESP32 [part_number=ESP32S-PIN30]

nets:
  GND: Grove1.GND, U1.GND
  VCC: Grove1.VCC, U1.3V3
  N1: Grove1.SDA, U1.D5
  N2: Grove1.SCL, U1.D23

custom parts:
  LuaNode32 / ESP32: New Image for LuaNode32 DOIT ESP32 DEVKIT V1. Base parts from LuaNode32 / ESP32 ESP32 based LuaNode32 by G.Noorlander DOIT Esp32 DevKit v1 (30 pins long, 11 pins width) by Werner Rothschopf (modified by vanepp Dec 2018)
