# Fritzing sketch fan (saved by Fritzing 0.9.3b)
breadboards: 1

parts:
  F1 = Fan - Ventilador [package=THT]
  U1 = LuaNode32 / ESP32 [part_number=ESP32S-PIN30]

nets:
  N1: F1.5V, U1.TX2
  GND: F1.GND, U1.GND

custom parts:
  Fan - Ventilador: Ventilador de 2 pines, se encuentra comunmente en computadoras de escritorio
  LuaNode32 / ESP32: New Image for LuaNode32 DOIT ESP32 DEVKIT V1. Base parts from LuaNode32 / ESP32 ESP32 based LuaNode32 by G.Noorlander DOIT Esp32 DevKit v1 (30 pins long, 11 pins width) by Werner Rothschopf (modified by vanepp Dec 2018)
