# Fritzing sketch flame sensor (saved by Fritzing 0.9.3b)
breadboards: 1

parts:
  S1 = KY-026
  U1 = LuaNode32 / ESP32 [part_number=ESP32S-PIN30]

nets:
  N1: S1.pin1, U1.D34
  N2: S1.pin2, U1.GND
  N3: S1.pin3, U1.3V3

custom parts:
  KY-026: ky-026 flame sensor module
  LuaNode32 / ESP32: New Image for LuaNode32 DOIT ESP32 DEVKIT V1. Base parts from LuaNode32 / ESP32 ESP32 based LuaNode32 by G.Noorlander DOIT Esp32 DevKit v1 (30 pins long, 11 pins width) by Werner Rothschopf (modified by vanepp Dec 2018)
