# Fritzing sketch ldr (saved by Fritzing 0.9.3b)
breadboards: 1

parts:
  R2 = Resistor [tolerance=±5% resistance=220 package="2010 [SMD]"]
  U1 = LuaNode32 / ESP32 [part_number=ESP32S-PIN30]
  R1 = Photocell (LDR) [package=THT]

nets:
  N1: R2.Pin_0, U1.D34, R1.pin_0
  N2: R2.Pin_1, U1.GND
  N3: U1.3V3, R1.pin_1

custom parts:
  LuaNode32 / ESP32: New Image for LuaNode32 DOIT ESP32 DEVKIT V1. Base parts from LuaNode32 / ESP32 ESP32 based LuaNode32 by G.Noorlander DOIT Esp32 DevKit v1 (30 pins long, 11 pins width) by Werner Rothschopf (modified by vanepp Dec 2018)
