# Fritzing sketch rotary (saved by Fritzing 0.9.3b)
breadboards: 1

parts:
  R1 = Resistor [tolerance=±5% resistance=220 package=THT]
  R2 = Resistor [tolerance=±5% resistance=220 package="2512 [SMD]"]
  U1 = LuaNode32 / ESP32 [part_number=ESP32S-PIN30]
  SW1 = ENCODER_RGB_CA [package=encoder_led_3]

nets:
  N1: R1.Pin_0, SW1.-G
  N2: R1.Pin_1, R2.Pin_1
  N3: R2.Pin_0, SW1.-R
  N4: U1.D35, SW1.B
  N5: U1.D25, SW1.A
  N6: U1.3V3, SW1.+
  N7: U1.GND, SW1.-B
  N8: U1.D21, SW1.C

custom parts:
  LuaNode32 / ESP32: New Image for LuaNode32 DOIT ESP32 DEVKIT V1. Base parts from LuaNode32 / ESP32 ESP32 based LuaNode32 by G.Noorlander DOIT Esp32 DevKit v1 (30 pins long, 11 pins width) by Werner Rothschopf (modified by vanepp Dec 2018)
