# Fritzing sketch sr04 (saved by Fritzing 0.9.3b)
breadboards: 1

parts:
  hc-sr1 = hc-sr04
  U1 = LuaNode32 / ESP32 [part_number=ESP32S-PIN30]

nets:
  VCC: hc-sr1.VCC, U1.3V3
  N1: hc-sr1.Trig, U1.D12
  N2: hc-sr1.Echo, U1.D13
  GND: hc-sr1.GND, U1.GND

custom parts:
  LuaNode32 / ESP32: New Image for LuaNode32 DOIT ESP32 DEVKIT V1. Base parts from LuaNode32 / ESP32 ESP32 based LuaNode32 by G.Noorlander DOIT Esp32 DevKit v1 (30 pins long, 11 pins width) by Werner Rothschopf (modified by vanepp Dec 2018)
