# Fritzing sketch stepper motor (saved by Fritzing 0.9.3b)
breadboards: 1

parts:
  SM1 = 28BYJ-48 Stepper Motor [part_number=28BYJ-48]
  U1 = LuaNode32 / ESP32 [part_number=ESP32S-PIN30]

nets:
  N1: SM1.blue-pin, U1.D19
  N2: SM1.pink-pin, U1.D18
  N3: SM1.yellow-pin, U1.D5
  N4: SM1.orange-pin, U1.TX2

custom parts:
  28BYJ-48 Stepper Motor: Unipolar Stepper Motor 28BYJ-48 Top coil - pink & orange Bottom coil - blue & yellow Common rail - red Connector pins: blue - pink - yellow - orange - red
  LuaNode32 / ESP32: New Image for LuaNode32 DOIT ESP32 DEVKIT V1. Base parts from LuaNode32 / ESP32 ESP32 based LuaNode32 by G.Noorlander DOIT Esp32 DevKit v1 (30 pins long, 11 pins width) by Werner Rothschopf (modified by vanepp Dec 2018)
