# Fritzing sketch touch piezzo sensor (saved by Fritzing 0.9.3b)
breadboards: 1

parts:
  U1 = LuaNode32 / ESP32 [part_number=ESP32S-PIN30]
  Piezoelectric_Sensor2 = Piezoelectric Sensor

nets:
  N1: U1.D33, Piezoelectric_Sensor2.VCC
  GND: U1.GND, Piezoelectric_Sensor2.GND

custom parts:
  LuaNode32 / ESP32: New Image for LuaNode32 DOIT ESP32 DEVKIT V1. Base parts from LuaNode32 / ESP32 ESP32 based LuaNode32 by G.Noorlander DOIT Esp32 DevKit v1 (30 pins long, 11 pins width) by Werner Rothschopf (modified by vanepp Dec 2018)
  Piezoelectric Sensor: Piezoelectric sensor.
